# Fritzing sketch CNC_ESP32 (saved by Fritzing 0.8.7b)
breadboards: 1

parts:
  M1 = DOIT Esp32 DevKit v1 (30 pins long, 11 pins width) [part_number=ESP32S-PIN30]
  MOTOR1 = 28BYJ-48 Stepper Motor
  BREAKOUT1 = ULN2003A breakout board
  MOTOR2 = 28BYJ-48 Stepper Motor
  BREAKOUT2 = ULN2003A breakout board
  J1 = Basic Servo
  JACK1 = 2.1mm Barrel Jack with Terminal Block

nets:
  3V3: M1.3V3, J1.vcc
  GND: M1.GND, J1.gnd
  N1: M1.D4, J1.pulse
  N2: M1.D32, BREAKOUT2.In_4
  N3: M1.D33, BREAKOUT2.In_3
  N4: M1.D25, BREAKOUT2.In_2
  N5: M1.D26, BREAKOUT2.In_1
  N6: M1.D27, BREAKOUT1.In_4
  N7: M1.D14, BREAKOUT1.In_3
  N8: M1.D12, BREAKOUT1.In_2
  N9: M1.D13, BREAKOUT1.In_1
  N10: MOTOR1.RED, BREAKOUT1.BLUE_wire
  N11: MOTOR1.ORANGE, BREAKOUT1.PINK_wire
  N12: MOTOR1.YELLOW, BREAKOUT1.YELLOW_wire
  N13: MOTOR1.PINK, BREAKOUT1.ORANGE_wire
  N14: MOTOR1.BLUE, BREAKOUT1.RED_wire
  N15: BREAKOUT1.0V, BREAKOUT2.0V, JACK1.NEG
  +5V: BREAKOUT1.+5V, BREAKOUT2.+5V, JACK1.POS
  N16: MOTOR2.RED, BREAKOUT2.BLUE_wire
  N17: MOTOR2.ORANGE, BREAKOUT2.PINK_wire
  N18: MOTOR2.YELLOW, BREAKOUT2.YELLOW_wire
  N19: MOTOR2.PINK, BREAKOUT2.ORANGE_wire
  N20: MOTOR2.BLUE, BREAKOUT2.RED_wire

notes:
  Pen Servo Z
  28BYJ-48 Axis X
  28BYJ-48 Axis Y
  ULN2003 Axis X
  ULN2003 Axis Y
  CNC ESP32 - 30 pins
  Attention: use external 5v power supply for stepper motors!
  5v
  3.3v

custom parts:
  DOIT Esp32 DevKit v1 (30 pins long, 11 pins width): The DOIT Esp32 DevKit v1 is one of the development board created by DOIT to evaluate the ESP-WROOM-32 module. It is based on the ESP32 microcontroller that boasts Wifi, Bluetooth, Ethernet and Low Power support all in a single chip. (vanepp) made breadboard work, adjusted pin numbering and labels and reduced size of schematic and cleaned up pcb. This chip is 30pins long (2 x15) and 11 pins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
  ULN2003A breakout board: ULN2003A 7-way Darlington Transistor Driver on breakoutboard
