# Fritzing sketch ladysteel (saved by Fritzing 0.9.3b)
breadboards: 1

parts:
  R1 = Resistor [tolerance=±5% resistance=10 package="1206 [SMD]"]
  LED_RGB = RGB LED (com. cathode, rbg) [package="5 mm [THT]"]
  Módulo_GPS = SUP500F [package=sup500f]
  R2 = Resistor [tolerance=±5% resistance=10 package="1206 [SMD]"]
  R3 = Resistor [tolerance=±5% resistance=10 package="1206 [SMD]"]
  PushButton = KY-004 Key Switch Module [package="Breakout board"]
  R4 = Resistor [tolerance=±5% resistance=100 package="1206 [SMD]"]
  part = DOIT Esp32 DevKit v1 (30 pins long, 11 pins width) [part_number=ESP32S-PIN30]

nets:
  N1: R1.Pin_0, part.TX2
  N2: R1.Pin_1, LED_RGB.green_anode
  N3: LED_RGB.red_anode, R2.Pin_1
  GND: LED_RGB.common_cathode, Módulo_GPS.GND, R4.Pin_0, part.GND
  N4: LED_RGB.blue_anode, R3.Pin_1
  N5: Módulo_GPS.RX-I, part.TX0
  N6: Módulo_GPS.TX-O, part.RX0
  VCC: Módulo_GPS.VCC, PushButton.S, part.3V3
  N7: R2.Pin_0, part.D18
  N8: R3.Pin_0, part.D5
  N9: PushButton.Vin, part.D19
  N10: PushButton.-, R4.Pin_1

notes:
  GND: Black
  VCC: Red
  RX: Yellow
  TX: Green

custom parts:
  KY-004 Key Switch Module: Arduino Key Switch Module Keyes KY-004 is a push button that will output a high signal when pressed.
  DOIT Esp32 DevKit v1 (30 pins long, 11 pins width): The DOIT Esp32 DevKit v1 is one of the development board created by DOIT to evaluate the ESP-WROOM-32 module. It is based on the ESP32 microcontroller that boasts Wifi, Bluetooth, Ethernet and Low Power support all in a single chip. (vanepp) made breadboard work, adjusted pin numbering and labels and reduced size of schematic and cleaned up pcb. This chip is 30pins long (2 x15) and 11 pins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
